// Logisim project molor_basic_processor.circ as structural Verilog: 3 circuits, main circuit cpu
module cpu (
  input  [31:0] INST,
  input  CLK,
  output [31:0] PC,
  output [31:0] MP,
  output WE,
  output RE
);

  wire [31:0] adder_1_out;

  Demultiplexer #(.select(2)) demultiplexer_1 (.in(1'b1), .sel(INST[1:0]));  // open: out0, out1, out2, out3
  Adder #(.width(32)) adder_1 (.a(PC), .b(32'h4), .out(adder_1_out));  // open: cin, cout
  register_memory register_memory_1 (
    .CLK(CLK), .PCin(adder_1_out), .PCWE(1'b1), .PC(PC), .Q(MP));  // open: DATA, SLC, WE, RST
endmodule

module register_memory (
  input  [31:0] DATA,
  input  [3:0] SLC,
  input  WE,
  input  CLK,
  input  RST,
  input  [31:0] PCin,
  input  PCWE,
  output [31:0] PC,
  output [31:0] Q
);

  wire demultiplexer_1_out0, demultiplexer_1_out1, demultiplexer_1_out2, demultiplexer_1_out3,
       demultiplexer_1_out4, demultiplexer_1_out5, demultiplexer_1_out6, demultiplexer_1_out7,
       demultiplexer_1_out8, demultiplexer_1_out9, demultiplexer_1_out10, demultiplexer_1_out11,
       demultiplexer_1_out12, demultiplexer_1_out13, demultiplexer_1_out14, or_2_out;
  wire [31:0] or_1_out, register_1_q, register_2_q, register_3_q, register_4_q, register_5_q, register_6_q,
       register_7_q, register_8_q, register_9_q, register_10_q, register_11_q, register_13_q, register_14_q,
       register_15_q;

  Demultiplexer #(.select(4)) demultiplexer_1 (
    .out0(demultiplexer_1_out0), .out1(demultiplexer_1_out1), .out2(demultiplexer_1_out2),
    .out3(demultiplexer_1_out3), .out4(demultiplexer_1_out4), .out5(demultiplexer_1_out5),
    .out6(demultiplexer_1_out6), .out7(demultiplexer_1_out7), .out8(demultiplexer_1_out8),
    .out9(demultiplexer_1_out9), .out10(demultiplexer_1_out10), .out11(demultiplexer_1_out11),
    .out12(demultiplexer_1_out12), .out13(demultiplexer_1_out13), .out14(demultiplexer_1_out14), .in(WE),
    .sel(SLC));  // open: out15
  Register #(.width(32)) register_1 (.D(DATA), .en(demultiplexer_1_out0), .clk(CLK), .Q(register_1_q), .clr(RST));
  Register #(.width(32)) register_2 (.D(DATA), .en(demultiplexer_1_out1), .clk(CLK), .Q(register_2_q), .clr(RST));
  Register #(.width(32)) register_3 (.D(DATA), .en(demultiplexer_1_out2), .clk(CLK), .Q(register_3_q), .clr(RST));
  Register #(.width(32)) register_4 (.D(DATA), .en(demultiplexer_1_out3), .clk(CLK), .Q(register_4_q), .clr(RST));
  Register #(.width(32)) register_5 (.D(DATA), .en(demultiplexer_1_out4), .clk(CLK), .Q(register_5_q), .clr(RST));
  Register #(.width(32)) register_6 (.D(DATA), .en(demultiplexer_1_out5), .clk(CLK), .Q(register_6_q), .clr(RST));
  Register #(.width(32)) register_7 (.D(DATA), .en(demultiplexer_1_out6), .clk(CLK), .Q(register_7_q), .clr(RST));
  Register #(.width(32)) register_8 (.D(DATA), .en(demultiplexer_1_out7), .clk(CLK), .Q(register_8_q), .clr(RST));
  Register #(.width(32)) register_9 (.D(DATA), .en(demultiplexer_1_out8), .clk(CLK), .Q(register_9_q), .clr(RST));
  Register #(.width(32)) register_10 (.D(DATA), .en(demultiplexer_1_out9), .clk(CLK), .Q(register_10_q), .clr(RST));
  Register #(.width(32)) register_11 (.D(DATA), .en(demultiplexer_1_out10), .clk(CLK), .Q(register_11_q), .clr(RST));
  Register #(.width(32)) register_12 (.D(or_1_out), .en(or_2_out), .clk(CLK), .Q(PC), .clr(RST));
  assign or_1_out = DATA | PCin;  // OR_Gate or_1, 32 bits wide
  or or_2 (or_2_out, demultiplexer_1_out10, PCWE);
  Register #(.width(32)) register_13 (.D(DATA), .en(demultiplexer_1_out12), .clk(CLK), .Q(register_13_q), .clr(RST));
  Register #(.width(32)) register_14 (.D(DATA), .en(demultiplexer_1_out13), .clk(CLK), .Q(register_14_q), .clr(RST));
  Register #(.width(32)) register_15 (.D(DATA), .en(demultiplexer_1_out14), .clk(CLK), .Q(register_15_q), .clr(RST));
  Multiplexer #(.select(4), .width(32)) multiplexer_1 (
    .in0(register_1_q), .in1(register_2_q), .in2(register_3_q), .in3(register_4_q), .in4(register_5_q),
    .in5(register_6_q), .in6(register_7_q), .in7(register_8_q), .in8(register_9_q), .in9(register_10_q),
    .in10(register_11_q), .in11(PC), .in12(register_13_q), .in13(register_14_q), .in14(register_15_q),
    .in15({32{1'b0}}), .out(Q), .sel(SLC));
endmodule

module main (
);

  wire clock_1_out, cpu_1_re, cpu_1_we;
  wire [15:0] bit_extender_1_out;
  wire [31:0] cpu_1_pc, rom_1_data;

  Clock clock_1 (.out(clock_1_out));
  RAM #(.addrWidth(16), .dataWidth(32)) ram_1 (
    .we(cpu_1_we), .oe(cpu_1_re), .clk(clock_1_out));  // open: addr, din, dout
  Bit_Extender #(.in_width(32)) bit_extender_1 (.in(cpu_1_pc), .out(bit_extender_1_out));
  ROM #(.addrWidth(16), .dataWidth(32)) rom_1 (.addr(bit_extender_1_out), .data(rom_1_data));
  cpu cpu_1 (.INST(rom_1_data), .CLK(clock_1_out), .PC(cpu_1_pc), .WE(cpu_1_we), .RE(cpu_1_re));  // open: MP
endmodule
